# Fritzing sketch 433Mhz_Receiver-Sketch (saved by Fritzing 0.9.2b)
breadboards: 1

parts:
  Bauteil3 = Arduino Nano (Rev3.0) (ICSP)
  <<_MX-05V = IC, SIP package, 4 pins [chip_label=REC.]

nets:
  N1: Bauteil3.GND, <<_MX-05V.pin4
  N2: Bauteil3.D3, <<_MX-05V.pin2
  N3: Bauteil3.5V, <<_MX-05V.pin1
