# Fritzing sketch Pi2_Shield-Sketch (saved by Fritzing 0.9.2b)
breadboards: 1

parts:
  Raspberry_Pi1 = Raspberry Pi 2
  J1 = Screw terminal - 2 pins [package=THT]
  J2 = Screw terminal - 2 pins [package=THT]
  LED1 = smd LED [color="Red (633nm)" package="1206 [SMD]"]
  J3 = Screw terminal - 2 pins [package=THT]
  R1 = Resistor [tolerance=±5% resistance=1k package="2010 [SMD]"]
  R2 = Resistor [tolerance=±5% resistance=10k package="2010 [SMD]"]
  R3 = Resistor [tolerance=±5% resistance=220 package="2010 [SMD]"]

nets:
  N1: Raspberry_Pi1.GPIO2, J2.pin1
  N2: Raspberry_Pi1.GPIO3, J2.pin2
  N3: Raspberry_Pi1.GPIO4, R1.Pin_1
  N4: Raspberry_Pi1.GPIO22, LED1.cathode
  N5: Raspberry_Pi1.GND, J1.pin2
  N6: Raspberry_Pi1.5V, R2.Pin_0, R3.Pin_0
  N7: LED1.anode, R3.Pin_1
  N8: J3.pin1, R1.Pin_0, R2.Pin_1
