# Fritzing sketch T&H_Sensor-Sketch (saved by Fritzing 0.9.2b)
circuit board: 8.46667cm x 5.64444cm
breadboards: 1

parts:
  C2 = Ceramic Capacitor [capacitance=100nF voltage=5V package="100 mil [THT, multilayer]"]
  RHT1 = Humidity and Temperature Sensor RHT03
  C3 = Electrolytic Capacitor [capacitance=1µF package="100 mil [THT, electrolytic]"]
  R1 = Resistor [tolerance=±5% resistance=4.7k package=THT]
  D1 = Rectifier Diode [part_number=1N4001 package="300 mil [THT]"]
  Bauteil3 = Arduino Nano (Rev3.0) (ICSP)

nets:
  N1: C2.0, RHT1.GND_2, C3.-, Bauteil3.GND
  N2: C2.1, RHT1.Vcc, C3.+, R1.Pin_1, D1.cathode
  N3: RHT1.Data-signal, R1.Pin_0, Bauteil3.D2
  N4: D1.anode, Bauteil3.5V
