# Fritzing sketch T&H_Sensor_With_433Mhz_Sender-Sketch (saved by Fritzing 0.9.2b)
breadboards: 1

parts:
  D1 = Rectifier Diode [part_number=1N4001 package="300 mil [THT]"]
  Bauteil3 = Arduino Nano (Rev3.0) (ICSP)
  RHT2 = Humidity and Temperature Sensor RHT03
  C4 = Electrolytic Capacitor [capacitance=1µF package="100 mil [THT, electrolytic]"]
  C5 = Ceramic Capacitor [capacitance=100nF voltage=5V package="100 mil [THT, multilayer]"]
  R2 = Resistor [tolerance=±5% resistance=4.7k package=THT]
  <<_MX-FS-03V = IC, SIP package, 3 pins [chip_label=SEND]
  C6 = Ceramic Capacitor [capacitance=100nF voltage=5V package="100 mil [THT, multilayer]"]

nets:
  N1: D1.cathode, RHT2.Vcc, C4.+, C5.0, R2.Pin_1
  N2: D1.anode, Bauteil3.5V, <<_MX-FS-03V.pin2, C6.1
  N3: Bauteil3.GND, RHT2.GND_2, C4.-, C5.1, <<_MX-FS-03V.pin3, C6.0
  N4: Bauteil3.D2, <<_MX-FS-03V.pin1
  N5: Bauteil3.D6, RHT2.Data-signal, R2.Pin_0
